// Logisim project 4BitCPU.circ as structural Verilog: 1 circuit, main circuit main
module main (
  input  [15:0] INSTRUCTION,
  output [3:0] out_2
);

  wire and_1_out, and_2_out, and_3_out, and_4_out, and_5_out, and_6_out, and_7_out, and_8_out, clock_1_out,
       not_1_out, not_2_out, not_3_out, not_4_out;
  wire [3:0] multiplexer_1_out, multiplexer_2_out, r0_q, r1_q, r2_q, r3_q;

  Clock clock_1 (.out(clock_1_out));
  not not_1 (not_1_out, INSTRUCTION[2]);
  and and_1 (and_1_out, not_1_out, not_2_out);
  not not_2 (not_2_out, INSTRUCTION[3]);
  and and_2 (and_2_out, INSTRUCTION[2], not_3_out);
  not not_3 (not_3_out, INSTRUCTION[3]);
  not not_4 (not_4_out, INSTRUCTION[2]);
  and and_3 (and_3_out, not_4_out, INSTRUCTION[3]);
  and and_4 (and_4_out, INSTRUCTION[2], INSTRUCTION[3]);
  Register #(.width(4)) r0 (.D(out_2), .en(and_5_out), .clk(clock_1_out), .Q(r0_q));  // open: clr
  and and_5 (and_5_out, INSTRUCTION[15], and_1_out);
  Register #(.width(4)) r1 (.D(out_2), .en(and_6_out), .clk(clock_1_out), .Q(r1_q));  // open: clr
  and and_6 (and_6_out, INSTRUCTION[15], and_2_out);
  Register #(.width(4)) r2 (.D(out_2), .en(and_7_out), .clk(clock_1_out), .Q(r2_q));  // open: clr
  and and_7 (and_7_out, INSTRUCTION[15], and_3_out);
  Register #(.width(4)) r3 (.D(out_2), .en(and_8_out), .clk(clock_1_out), .Q(r3_q));  // open: clr
  and and_8 (and_8_out, INSTRUCTION[15], and_4_out);
  Multiplexer #(.select(2), .width(4)) multiplexer_1 (
    .in0(r0_q), .in1(r1_q), .in2(r2_q), .in3(r3_q), .out(multiplexer_1_out), .sel(INSTRUCTION[1:0]));
  Multiplexer #(.select(2), .width(4)) multiplexer_2 (
    .in0(r0_q), .in1(r1_q), .in2(r2_q), .in3(r3_q), .out(multiplexer_2_out), .sel(INSTRUCTION[3:2]));
  Adder #(.width(4)) adder_1 (.a(multiplexer_1_out), .b(multiplexer_2_out), .out(out_2));  // open: cin, cout
  RAM #(.dataWidth(16)) instructionmem (.clk(clock_1_out));  // open: addr, we, oe, din, dout
  Adder #(.width(4)) adder_2 ();  // open: a, b, out, cin, cout
  Subtractor #(.width(4)) subtractor_1 ();  // open: a, b, out, bin, bout
endmodule
